# Fritzing sketch 7X7X7_richtig (saved by Fritzing 0.9.10b)
circuit board: 16.02cm x 10.02cm
perfboards: 1

parts:
  74HC574 = IC, DIP package, 20 pins [chip_label=745HC574]
  74HC574_2 = 74HC574 [package="DIP (Dual Inline) [THT]"]
  74HC574_3 = 74HC574 [package="DIP (Dual Inline) [THT]"]
  74HC574_4 = 74HC574 [package="DIP (Dual Inline) [THT]"]
  74HC574_5 = 74HC574 [package="DIP (Dual Inline) [THT]"]
  74HC574_6 = 74HC574 [package="DIP (Dual Inline) [THT]"]
  74HC574_7 = 74HC574 [package="DIP (Dual Inline) [THT]"]
  R1 = Resistor [tolerance=±5% power=0.25 resistance=220 package=THT]
  R2 = Resistor [tolerance=±5% power=0.25 resistance=220 package=THT]
  R3 = Resistor [tolerance=±5% power=0.25 resistance=220 package=THT]
  R4 = Resistor [tolerance=±5% power=0.25 resistance=220 package=THT]
  R5 = Resistor [tolerance=±5% power=0.25 resistance=220 package=THT]
  R6 = Resistor [tolerance=±5% power=0.25 resistance=220 package=THT]
  R7 = Resistor [tolerance=±5% power=0.25 resistance=220 package=THT]
  R8 = Resistor [tolerance=±5% power=0.25 resistance=220 package=THT]
  R9 = Resistor [tolerance=±5% power=0.25 resistance=220 package=THT]
  R10 = Resistor [tolerance=±5% power=0.25 resistance=220 package=THT]
  R11 = Resistor [tolerance=±5% power=0.25 resistance=220 package=THT]
  R12 = Resistor [tolerance=±5% power=0.25 resistance=220 package=THT]
  R13 = Resistor [tolerance=±5% power=0.25 resistance=220 package=THT]
  R14 = Resistor [tolerance=±5% power=0.25 resistance=220 package=THT]
  R15 = Resistor [tolerance=±5% power=0.25 resistance=220 package=THT]
  R16 = Resistor [tolerance=±5% power=0.25 resistance=220 package=THT]
  R17 = Resistor [tolerance=±5% power=0.25 resistance=220 package=THT]
  R18 = Resistor [tolerance=±5% power=0.25 resistance=220 package=THT]
  R19 = Resistor [tolerance=±5% power=0.25 resistance=220 package=THT]
  R20 = Resistor [tolerance=±5% power=0.25 resistance=220 package=THT]
  R21 = Resistor [tolerance=±5% power=0.25 resistance=220 package=THT]
  R22 = Resistor [tolerance=±5% power=0.25 resistance=220 package=THT]
  R23 = Resistor [tolerance=±5% power=0.25 resistance=220 package=THT]
  R24 = Resistor [tolerance=±5% power=0.25 resistance=220 package=THT]
  R25 = Resistor [tolerance=±5% power=0.25 resistance=220 package=THT]
  R26 = Resistor [tolerance=±5% power=0.25 resistance=220 package=THT]
  R27 = Resistor [tolerance=±5% power=0.25 resistance=220 package=THT]
  R28 = Resistor [tolerance=±5% power=0.25 resistance=220 package=THT]
  R29 = Resistor [tolerance=±5% power=0.25 resistance=220 package=THT]
  R30 = Resistor [tolerance=±5% power=0.25 resistance=220 package=THT]
  R31 = Resistor [tolerance=±5% power=0.25 resistance=220 package=THT]
  R32 = Resistor [tolerance=±5% power=0.25 resistance=220 package=THT]
  R33 = Resistor [tolerance=±5% power=0.25 resistance=220 package=THT]
  R34 = Resistor [tolerance=±5% power=0.25 resistance=220 package=THT]
  R35 = Resistor [tolerance=±5% power=0.25 resistance=220 package=THT]
  R36 = Resistor [tolerance=±5% power=0.25 resistance=220 package=THT]
  R37 = Resistor [tolerance=±5% power=0.25 resistance=220 package=THT]
  R38 = Resistor [tolerance=±5% power=0.25 resistance=220 package=THT]
  R39 = Resistor [tolerance=±5% power=0.25 resistance=220 package=THT]
  R40 = Resistor [tolerance=±5% power=0.25 resistance=220 package=THT]
  R41 = Resistor [tolerance=±5% power=0.25 resistance=220 package=THT]
  R42 = Resistor [tolerance=±5% power=0.25 resistance=220 package=THT]
  R43 = Resistor [tolerance=±5% power=0.25 resistance=220 package=THT]
  J1 = female pin header, 7 pins [form="♀ (female)"]
  J2 = female pin header, 7 pins [form="♀ (female)"]
  J3 = female pin header, 7 pins [form="♀ (female)"]
  J4 = female pin header, 7 pins [form="♀ (female)"]
  J5 = female pin header, 7 pins [form="♀ (female)"]
  J6 = female pin header, 7 pins [form="♀ (female)"]
  J7 = female pin header, 7 pins [form="♀ (female)"]
  R44 = Resistor [tolerance=±5% power=0.25 resistance=220 package=THT]
  R45 = Resistor [tolerance=±5% power=0.25 resistance=220 package=THT]
  R46 = Resistor [tolerance=±5% power=0.25 resistance=220 package=THT]
  R47 = Resistor [tolerance=±5% power=0.25 resistance=220 package=THT]
  R48 = Resistor [tolerance=±5% power=0.25 resistance=220 package=THT]
  R49 = Resistor [tolerance=±5% power=0.25 resistance=220 package=THT]
  S1 = Pushbutton [package="[THT]"]
  R50 = Resistor [tolerance=±5% power=0.25 resistance=10k package=THT]
  74HC138 = IC, DIP package, 16 pins [chip_label=74HC138]
  C1 = Ceramic Capacitor [capacitance=0.22nF voltage=35V package="100 mil [THT, multilayer]"]
  C2 = Ceramic Capacitor [capacitance=2.2nF voltage=35V package="100 mil [THT, multilayer]"]
  XTAL1 = Crystal [frequency="16 Mhz" package=THT]
  Q1 = NPN-Transistor [package="TO92 [THT]"]
  R51 = Resistor [tolerance=±5% power=0.25 resistance=1k package=THT]
  R52 = Resistor [tolerance=±5% power=0.25 resistance=1k package=THT]
  R53 = Resistor [tolerance=±5% power=0.25 resistance=1k package=THT]
  R54 = Resistor [tolerance=±5% power=0.25 resistance=1k package=THT]
  R55 = Resistor [tolerance=±5% power=0.25 resistance=1k package=THT]
  R56 = Resistor [tolerance=±5% power=0.25 resistance=1k package=THT]
  R57 = Resistor [tolerance=±5% power=0.25 resistance=1k package=THT]
  Q2 = NPN-Transistor [package="TO92 [THT]"]
  Q3 = NPN-Transistor [package="TO92 [THT]"]
  Q4 = NPN-Transistor [package="TO92 [THT]"]
  Q5 = NPN-Transistor [package="TO92 [THT]"]
  Q6 = NPN-Transistor [package="TO92 [THT]"]
  Q7 = NPN-Transistor [package="TO92 [THT]"]
  J8 = female pin header, 1 pin [form="♀ (female)"]
  J9 = female pin header, 1 pin [form="♀ (female)"]
  J10 = female pin header, 1 pin [form="♀ (female)"]
  J11 = female pin header, 1 pin [form="♀ (female)"]
  J12 = female pin header, 1 pin [form="♀ (female)"]
  J13 = female pin header, 1 pin [form="♀ (female)"]
  J14 = female pin header, 1 pin [form="♀ (female)"]
  J15 = Screw terminal - 2 pins [package=THT]
  ATmega_328p = atmega328 [package=dip]
  C7 = Ceramic Capacitor [capacitance=100nF voltage=35V package="100 mil [THT, multilayer]"]
  C6 = Ceramic Capacitor [capacitance=100nF voltage=35V package="100 mil [THT, multilayer]"]
  C5 = Ceramic Capacitor [capacitance=100nF voltage=35V package="100 mil [THT, multilayer]"]
  C4 = Ceramic Capacitor [capacitance=100nF voltage=35V package="100 mil [THT, multilayer]"]
  C3 = Ceramic Capacitor [capacitance=100nF voltage=35V package="100 mil [THT, multilayer]"]
  C9 = Ceramic Capacitor [capacitance=100nF voltage=35V package="100 mil [THT, multilayer]"]
  C8 = Ceramic Capacitor [capacitance=100nF voltage=35V package="100 mil [THT, multilayer]"]
  C10 = Ceramic Capacitor [capacitance=100nF voltage=35V package="100 mil [THT, multilayer]"]
  C11 = Ceramic Capacitor [capacitance=100nF voltage=35V package="100 mil [THT, multilayer]"]

nets:
  GND: 74HC574.pin1, 74HC574.pin10, 74HC574_2.-QE, 74HC574_2.GND, 74HC574_3.-QE, 74HC574_3.GND, 74HC574_4.-QE, 74HC574_4.GND, 74HC574_5.-QE, 74HC574_5.GND, 74HC574_6.-QE, 74HC574_6.GND, 74HC574_7.-QE, 74HC574_7.GND, S1.Pin_3, S1.Pin_4, 74HC138.pin4, 74HC138.pin5, 74HC138.pin8, C1.0, C2.0, Q1.E, Q2.E, Q3.E, Q4.E, Q5.E, Q6.E, Q7.E, J15.pin1, ATmega_328p.GND, C7.1, C6.1, C5.1, C4.1, C3.1, C9.1, C8.1, C10.0, C11.0
  N1: 74HC574.pin2, 74HC574_2.D1, 74HC574_3.D1, 74HC574_4.D1, 74HC574_5.D1, 74HC574_6.D1, 74HC574_7.D1, ATmega_328p.D0_(RX)
  N2: 74HC574.pin3, 74HC574_2.D2, 74HC574_3.D2, 74HC574_4.D2, 74HC574_5.D2, 74HC574_6.D2, 74HC574_7.D2, ATmega_328p.D1_(TX)
  N3: 74HC574.pin4, 74HC574_2.D3, 74HC574_3.D3, 74HC574_4.D3, 74HC574_5.D3, 74HC574_6.D3, 74HC574_7.D3, ATmega_328p.D2
  N4: 74HC574.pin5, 74HC574_2.D4, 74HC574_3.D4, 74HC574_4.D4, 74HC574_5.D4, 74HC574_6.D4, 74HC574_7.D4, ATmega_328p.D3_(PWM)
  N5: 74HC574.pin6, 74HC574_2.D5, 74HC574_3.D5, 74HC574_4.D5, 74HC574_5.D5, 74HC574_6.D5, 74HC574_7.D5, ATmega_328p.D4
  N6: 74HC574.pin7, 74HC574_2.6, 74HC574_3.6, 74HC574_4.6, 74HC574_5.6, 74HC574_6.6, 74HC574_7.6, ATmega_328p.D5_(PWM)
  N7: 74HC574.pin8, 74HC574_2.D7, 74HC574_3.D7, 74HC574_4.D7, 74HC574_5.D7, 74HC574_6.D7, 74HC574_7.D7, ATmega_328p.D6_(PWM)
  N8: 74HC574.pin11, 74HC138.pin15
  N9: 74HC574.pin13, R7.Pin_1
  N10: 74HC574.pin14, R6.Pin_1
  N11: 74HC574.pin15, R5.Pin_1
  N12: 74HC574.pin16, R4.Pin_1
  N13: 74HC574.pin17, R3.Pin_1
  N14: 74HC574.pin18, R2.Pin_1
  N15: 74HC574.pin19, R1.Pin_1
  VCC: 74HC574.pin20, 74HC574_2.VCC, 74HC574_3.VCC, 74HC574_4.VCC, 74HC574_5.VCC, 74HC574_6.VCC, 74HC574_7.VCC, R50.Pin_1, 74HC138.pin6, 74HC138.pin16, J15.pin2, ATmega_328p.VCC, ATmega_328p.AVCC, C7.0, C6.0, C5.0, C4.0, C3.0, C9.0, C8.0, C10.1, C11.1
  N16: 74HC574_2.CLK, 74HC138.pin14
  N17: 74HC574_2.Q7, R17.Pin_1
  N18: 74HC574_2.Q6, R8.Pin_1
  N19: 74HC574_2.Q5, R13.Pin_1
  N20: 74HC574_2.Q4, R9.Pin_1
  N21: 74HC574_2.Q3, R12.Pin_1
  N22: 74HC574_2.Q2, R10.Pin_1
  N23: 74HC574_2.Q1, R11.Pin_1
  N24: 74HC574_3.CLK, 74HC138.pin13
  N25: 74HC574_3.Q7, R22.Pin_1
  N26: 74HC574_3.Q6, R23.Pin_1
  N27: 74HC574_3.Q5, R14.Pin_1
  N28: 74HC574_3.Q4, R19.Pin_1
  N29: 74HC574_3.Q3, R15.Pin_1
  N30: 74HC574_3.Q2, R18.Pin_1
  N31: 74HC574_3.Q1, R16.Pin_1
  N32: 74HC574_4.CLK, 74HC138.pin12
  N33: 74HC574_4.Q7, R30.Pin_1
  N34: 74HC574_4.Q6, R28.Pin_1
  N35: 74HC574_4.Q5, R29.Pin_1
  N36: 74HC574_4.Q4, R20.Pin_1
  N37: 74HC574_4.Q3, R25.Pin_1
  N38: 74HC574_4.Q2, R21.Pin_1
  N39: 74HC574_4.Q1, R24.Pin_1
  N40: 74HC574_5.CLK, 74HC138.pin11
  N41: 74HC574_5.Q7, R35.Pin_1
  N42: 74HC574_5.Q6, R34.Pin_1
  N43: 74HC574_5.Q5, R33.Pin_1
  N44: 74HC574_5.Q4, R32.Pin_1
  N45: 74HC574_5.Q3, R26.Pin_1
  N46: 74HC574_5.Q2, R31.Pin_1
  N47: 74HC574_5.Q1, R27.Pin_1
  N48: 74HC574_6.CLK, 74HC138.pin10
  N49: 74HC574_6.Q7, R38.Pin_1
  N50: 74HC574_6.Q6, R41.Pin_1
  N51: 74HC574_6.Q5, R40.Pin_1
  N52: 74HC574_6.Q4, R42.Pin_1
  N53: 74HC574_6.Q3, R43.Pin_1
  N54: 74HC574_6.Q2, R37.Pin_1
  N55: 74HC574_6.Q1, R36.Pin_1
  N56: 74HC574_7.CLK, 74HC138.pin9
  N57: 74HC574_7.Q7, R49.Pin_1
  N58: 74HC574_7.Q6, R48.Pin_1
  N59: 74HC574_7.Q5, R47.Pin_1
  N60: 74HC574_7.Q4, R46.Pin_1
  N61: 74HC574_7.Q3, R45.Pin_1
  N62: 74HC574_7.Q2, R44.Pin_1
  N63: 74HC574_7.Q1, R39.Pin_1
  N64: R1.Pin_0, J1.pin1
  N65: R2.Pin_0, J1.pin2
  N66: R3.Pin_0, J1.pin3
  N67: R4.Pin_0, J1.pin4
  N68: R5.Pin_0, J1.pin5
  N69: R6.Pin_0, J1.pin6
  N70: R7.Pin_0, J1.pin7
  N71: R8.Pin_0, J2.pin6
  N72: R9.Pin_0, J2.pin4
  N73: R10.Pin_0, J2.pin2
  N74: R11.Pin_0, J2.pin1
  N75: R12.Pin_0, J2.pin3
  N76: R13.Pin_0, J2.pin5
  N77: R14.Pin_0, J3.pin5
  N78: R15.Pin_0, J3.pin3
  N79: R16.Pin_0, J3.pin1
  N80: R17.Pin_0, J2.pin7
  N81: R18.Pin_0, J3.pin2
  N82: R19.Pin_0, J3.pin4
  N83: R20.Pin_0, J4.pin4
  N84: R21.Pin_0, J4.pin2
  N85: R22.Pin_0, J3.pin7
  N86: R23.Pin_0, J3.pin6
  N87: R24.Pin_0, J4.pin1
  N88: R25.Pin_0, J4.pin3
  N89: R26.Pin_0, J5.pin3
  N90: R27.Pin_0, J5.pin1
  N91: R28.Pin_0, J4.pin6
  N92: R29.Pin_0, J4.pin5
  N93: R30.Pin_0, J4.pin7
  N94: R31.Pin_0, J5.pin2
  N95: R32.Pin_0, J5.pin4
  N96: R33.Pin_0, J5.pin5
  N97: R34.Pin_0, J5.pin6
  N98: R35.Pin_0, J5.pin7
  N99: R36.Pin_0, J6.pin1
  N100: R37.Pin_0, J6.pin2
  N101: R38.Pin_0, J6.pin7
  N102: R39.Pin_0, J7.pin1
  N103: R40.Pin_0, J6.pin5
  N104: R41.Pin_0, J6.pin6
  N105: R42.Pin_0, J6.pin4
  N106: R43.Pin_0, J6.pin3
  N107: J7.pin2, R44.Pin_0
  N108: J7.pin3, R45.Pin_0
  N109: J7.pin4, R46.Pin_0
  N110: J7.pin5, R47.Pin_0
  N111: J7.pin6, R48.Pin_0
  N112: J7.pin7, R49.Pin_0
  N113: S1.Pin_1, S1.Pin_2, R50.Pin_0, ATmega_328p.RESET
  N114: 74HC138.pin1, ATmega_328p.A2
  N115: 74HC138.pin2, ATmega_328p.A1
  N116: 74HC138.pin3, ATmega_328p.A0
  N117: C1.1, XTAL1.pin_0, ATmega_328p.XLAT1
  N118: C2.1, XTAL1.pin_1, ATmega_328p.XLAT2
  N119: Q1.B, R51.Pin_0
  N120: Q1.C, J8.pin1
  N121: R51.Pin_1, ATmega_328p.D7
  N122: R52.Pin_0, Q2.B
  N123: R52.Pin_1, ATmega_328p.D8
  N124: R53.Pin_0, Q7.B
  N125: R53.Pin_1, ATmega_328p.D13
  N126: R54.Pin_0, Q6.B
  N127: R54.Pin_1, ATmega_328p.D12
  N128: R55.Pin_0, Q5.B
  N129: R55.Pin_1, ATmega_328p.D11_(PWM)
  N130: R56.Pin_0, Q4.B
  N131: R56.Pin_1, ATmega_328p.D10_(PWM)
  N132: R57.Pin_0, Q3.B
  N133: R57.Pin_1, ATmega_328p.D9_(PWM)
  N134: Q2.C, J9.pin1
  N135: Q3.C, J10.pin1
  N136: Q4.C, J11.pin1
  N137: Q5.C, J12.pin1
  N138: Q6.C, J13.pin1
  N139: Q7.C, J14.pin1

notes:
  PCB designed by Kidiges
  Idea and original Plan by Marcazzan_M

custom parts:
  74HC574: A DIP stand-in part for whatever IC you want. With 20 pins on a 300mil dual inline package (DIP) footprint.

// code stored in the sketch: led_cube.ino
//This code represent the easiest animation for LED CUBE

int temp  = 50, cont = 0;

//This function loads all the cube
void load_all(void)  {
  //layer 1
  digitalWrite(A2, LOW);
  digitalWrite(A1, LOW);
  digitalWrite(A0,  LOW);
  delay(1);

  //layer 2
  digitalWrite(A2, HIGH);
  digitalWrite(A1,  LOW);
  digitalWrite(A0, LOW);
  delay(1);

  //layer 3
  digitalWrite(A2,  LOW);
  digitalWrite(A1, HIGH);
  digitalWrite(A0, LOW);
  delay(1);

  //layer 4
  digitalWrite(A2, HIGH);
  digitalWrite(A1, HIGH);
  digitalWrite(A0,  LOW);
  delay(1);

  //layer 5
  digitalWrite(A2, LOW);
  digitalWrite(A1,  LOW);
  digitalWrite(A0, HIGH);
  delay(1);

  //layer 6
  digitalWrite(A2,  HIGH);
  digitalWrite(A1, LOW);
  digitalWrite(A0, HIGH);
  delay(1);

  //layer 7
  digitalWrite(A2, LOW);
  digitalWrite(A1, HIGH);
  digitalWrite(A0,  HIGH);
  delay(1);

  //layer 8
  digitalWrite(A2, HIGH);
  digitalWrite(A1,  HIGH);
  digitalWrite(A0, HIGH);
  delay(1);

}

//This function  actives each layer one time and you can decide the time that the layer turns on
void  scrolling(int t) {
  PORTB = 0x00;
  digitalWrite(7, HIGH);
  delay(t);
  digitalWrite(7, LOW);

  digitalWrite(8, HIGH);
  delay(t);
  digitalWrite(8,  LOW);

  digitalWrite(9, HIGH);
  delay(t);
  digitalWrite(9, LOW);

  digitalWrite(10, HIGH);
  delay(t);
  digitalWrite(10, LOW);

  digitalWrite(11,  HIGH);
  delay(t);
  digitalWrite(11, LOW);

  digitalWrite(12, HIGH);
  delay(t);
  digitalWrite(12, LOW);

  digitalWrite(13, HIGH);
  delay(t);
  digitalWrite(13, LOW);

}

//This animation turns on one layer per  time, and it increases the speed of it, so finally you see all cube switched on
void  one(void) {
  PORTD = 0xff;
  load_all();
  while (1) {
    scrolling(temp);

    temp = temp - 2;

    if (temp <= 0) {
      temp = 1;
      cont++;
      if (cont == 1000) {
        cont = 0;
        temp = 100;
      }
    }

  }
}

void setup() {
  DDRD = 0xff;
  DDRB = 0xff;
  DDRC = 0xff;

}

void loop() {
  one();
}
